# Fritzing sketch HC_SR04 (saved by Fritzing 0.9.2b)

parts:
  Composant1 = Arduino Uno (Rev3)
  Composant2 = HC-SR04

nets:
  N1: Composant1.D8, Composant2.Trig
  N2: Composant1.D7, Composant2.Echo
  5V: Composant1.5V, Composant2.Vcc
  GND: Composant1.GND, Composant2.Gnd

custom parts:
  HC-SR04: HC-SR04 ultrasonic distance sensor
