# Fritzing sketch L293D (saved by Fritzing 0.9.2b)
breadboards: 1

parts:
  Composant1 = Arduino Uno (Rev3)
  IC1 = L293D [package=THT]
  M1 = DC Motor
  M2 = DC Motor
  VCC1 = Battery block 9V

nets:
  N1: Composant1.D8, IC1.In_4
  N2: Composant1.D2, IC1.In_1
  N3: Composant1.D4, IC1.In_2
  N4: Composant1.D5_PWM, IC1.Enable_1
  N5: Composant1.D6_PWM, IC1.Enable_2
  N6: Composant1.D7, IC1.In_3
  N7: Composant1.5V, IC1.+V
  N8: Composant1.GND, IC1.0V, VCC1.-
  N9: IC1.Out_1_(_Controlled_by_Enable_1_), M2.pin_2
  N10: IC1.Out_2_(_Controlled_by_Enable_1_), M2.pin_1
  N11: IC1.+Vmotor, VCC1.+
  N12: IC1.Out_3_(_Controlled_by_Enable_2_), M1.pin_2
  N13: IC1.Out_4_(_Controlled_by_Enable_2_), M1.pin_1

notes:
  Commande de deux MCC a l'aide d'un L293D
  Open Hardware Algerie
  Designer : Aidi Nour El Islam
  Licence :GPL V2
